// Logisim project eXORbitant.circ as structural Verilog: 1 circuit, main circuit main
module main (
  input  [15:0] KEEP_0,
  input  in_2,
  input  SET_TO_1_v1,
  input  RESET_COUNTER,
  input  SET_TO_1_v2,
  input  SET_TO_1_v3,
  input  in_7,
  input  in_8
);

  wire CLOCK_out;
  wire [15:0] counter_1_q, ram_1_data, rom_1_data;

  Clock CLOCK (.out(CLOCK_out));
  Counter #(.width(16), .max('hffff)) counter_1 (
    .load(in_2), .D(KEEP_0), .count(SET_TO_1_v1), .Q(counter_1_q), .clk(CLOCK_out), .clr(RESET_COUNTER));  // open: carry
  ROM #(.addrWidth(16), .dataWidth(16)) rom_1 (.addr(counter_1_q), .data(rom_1_data), .sel(SET_TO_1_v2));
  RAM #(.addrWidth(16), .dataWidth(16)) ram_1 (
    .addr(counter_1_q), .data(ram_1_data), .sel(SET_TO_1_v3), .clk(CLOCK_out), .ld(in_7), .clr(in_8));
  xor xor_1 (ram_1_data[15], rom_1_data[15], rom_1_data[13], rom_1_data[10], rom_1_data[9], rom_1_data[7], rom_1_data[6], rom_1_data[5], rom_1_data[2], rom_1_data[1]);
  xor xor_2 (ram_1_data[14], rom_1_data[15], rom_1_data[14], rom_1_data[9], rom_1_data[3], rom_1_data[2], rom_1_data[1]);
  xor xor_3 (ram_1_data[13], rom_1_data[14], rom_1_data[13], rom_1_data[12], rom_1_data[11], rom_1_data[10], rom_1_data[9], rom_1_data[7], rom_1_data[5], rom_1_data[4], rom_1_data[3], rom_1_data[1]);
  xor xor_4 (ram_1_data[12], rom_1_data[15], rom_1_data[14], rom_1_data[13], rom_1_data[12], rom_1_data[11], rom_1_data[8], rom_1_data[6], rom_1_data[5], rom_1_data[4], rom_1_data[3]);
  xor xor_5 (ram_1_data[11], rom_1_data[12], rom_1_data[11], rom_1_data[10], rom_1_data[6], rom_1_data[5], rom_1_data[2], rom_1_data[1]);
  xor xor_6 (ram_1_data[10], rom_1_data[15], rom_1_data[11], rom_1_data[9], rom_1_data[6], rom_1_data[3], rom_1_data[0]);
  xor xor_7 (ram_1_data[9], rom_1_data[14], rom_1_data[10], rom_1_data[9], rom_1_data[8], rom_1_data[7], rom_1_data[5], rom_1_data[4], rom_1_data[1], rom_1_data[0]);
  xor xor_8 (ram_1_data[8], rom_1_data[11], rom_1_data[10], rom_1_data[9], rom_1_data[8], rom_1_data[7], rom_1_data[6], rom_1_data[4], rom_1_data[2], rom_1_data[0]);
  xor xor_9 (ram_1_data[7], rom_1_data[15], rom_1_data[14], rom_1_data[12], rom_1_data[11], rom_1_data[9], rom_1_data[8], rom_1_data[7], rom_1_data[6], rom_1_data[5], rom_1_data[4], rom_1_data[2], rom_1_data[0]);
  xor xor_10 (ram_1_data[6], rom_1_data[15], rom_1_data[13], rom_1_data[12], rom_1_data[10], rom_1_data[9], rom_1_data[8], rom_1_data[6], rom_1_data[5], rom_1_data[1], rom_1_data[0]);
  xor xor_11 (ram_1_data[5], rom_1_data[11], rom_1_data[10], rom_1_data[7], rom_1_data[2]);
  xor xor_12 (ram_1_data[4], rom_1_data[14], rom_1_data[7], rom_1_data[6], rom_1_data[3]);
  xor xor_13 (ram_1_data[3], rom_1_data[15], rom_1_data[14], rom_1_data[13], rom_1_data[12], rom_1_data[11], rom_1_data[10], rom_1_data[9], rom_1_data[8], rom_1_data[5], rom_1_data[4], rom_1_data[3], rom_1_data[0]);
  xor xor_14 (ram_1_data[2], rom_1_data[15], rom_1_data[13], rom_1_data[7], rom_1_data[5], rom_1_data[3], rom_1_data[2], rom_1_data[1], rom_1_data[0]);
  xor xor_15 (ram_1_data[1], rom_1_data[15], rom_1_data[14], rom_1_data[11], rom_1_data[9], rom_1_data[7], rom_1_data[6], rom_1_data[5], rom_1_data[4], rom_1_data[1], rom_1_data[0]);
  xor xor_16 (ram_1_data[0], rom_1_data[14], rom_1_data[13], rom_1_data[12], rom_1_data[11], rom_1_data[9], rom_1_data[7], rom_1_data[5], rom_1_data[4], rom_1_data[3], rom_1_data[2]);

  // Notes on the sheet:
  //   Toggle to start encryption
  //   Input (Flag In Hex)
  //   Output (Encrypted)
endmodule
